// Digital circuit adder-subtractor.dig as structural Verilog
module adder_subtractor (
  input  [3:0] in_1,
  input  [3:0] A,
  input  [3:0] B,
  output [3:0] S
);

  wire add_1_c_o, add_2_c_o, add_3_c_o, xor_1_out, xor_2_out, xor_3_out, xor_4_out, xor_5_out;

  xor xor_1 (xor_1_out, 1'b0, in_1[2]);
  xor xor_2 (xor_2_out, B[0], in_1[2]);
  xor xor_3 (xor_3_out, B[1], in_1[2]);
  xor xor_4 (xor_4_out, B[2], in_1[2]);
  xor xor_5 (xor_5_out, B[3], in_1[2]);
  Add add_1 (.a(A[0]), .b(xor_2_out), .c_i(xor_1_out), .s(S[0]), .c_o(add_1_c_o));
  Add add_2 (.a(A[1]), .b(xor_3_out), .c_i(add_1_c_o), .s(S[1]), .c_o(add_2_c_o));
  Add add_3 (.a(A[2]), .b(xor_4_out), .c_i(add_2_c_o), .s(S[2]), .c_o(add_3_c_o));
  Add add_4 (.a(A[3]), .b(xor_5_out), .c_i(add_3_c_o), .s(S[3]));  // open: c_o
  // Pins of 1 and 4 bits meet at in_1
  // Pins of 1 and 4 bits meet at A
  // Pins of 1 and 4 bits meet at B
  // Pins of 1 and 4 bits meet at S
endmodule
